// Logisim project Computador- 8 bits- Tiago Defendi (a2571374) - 2023 - backup.circ as structural Verilog: 9 circuits, main circuit main
module main (
  input  [10:0] in_1,
  output [7:0] out_2
);

  wire \Botão , clock_1_out, or_1_out;
  wire [2:0] Contador, \memoria_11x8_1_saída_2 ;
  wire [7:0] \memoria_11x8_1_saída , ula_1_out_4;

  Clock clock_1 (.out(clock_1_out));
  contador0a7 contador0a7_1 (.Clock(clock_1_out), .\Saída (Contador));
  or or_1 (or_1_out, clock_1_out, \Botão );
  Button button_1 (.out(\Botão ));
  ULA ula_1 (.A(out_2), .B(\memoria_11x8_1_saída ), .Op(\memoria_11x8_1_saída_2 ), .out_4(ula_1_out_4));
  Registrador_8bits registrador_8bits_1 (.Entrada(ula_1_out_4), .Leitura_escrita(or_1_out), .\Saída (out_2));
  Memoria_11x8 memoria_11x8_1 (
    .Entrada(in_1), .\Endereço (Contador), .Leitura_Escrita(\Botão ),
    .\Saída ({\memoria_11x8_1_saída_2 , \memoria_11x8_1_saída }));
  Hex_Digit_Display hex_digit_display_1 (.value({1'b0, Contador}));  // open: dp

  // Notes on the sheet:
  //   000 - OR
  //   001 - AND
  //   010 - XOR
  //   011 - ADD
  //   100 - SUB
  //   101 - MUL
  //   110 - DIV
  //   111 - MOD
endmodule

module Operador (
  input  [2:0] \Operação ,
  output [7:0] out_2,
  output [7:0] out_3,
  output [7:0] out_4,
  output [7:0] out_5,
  output [7:0] out_6,
  output [7:0] out_7,
  output [7:0] out_8,
  output [7:0] out_9
);

  and and_1 (out_2[7], ~\Operação [2], ~\Operação [1], ~\Operação [0]);  // AND_Gate
  and and_2 (out_3[7], ~\Operação [2], ~\Operação [1], \Operação [0]);  // AND_Gate
  and and_3 (out_4[7], ~\Operação [2], \Operação [1], ~\Operação [0]);  // AND_Gate
  and and_4 (out_5[7], ~\Operação [2], \Operação [1], \Operação [0]);  // AND_Gate
  and and_5 (out_6[7], \Operação [2], ~\Operação [1], ~\Operação [0]);  // AND_Gate
  and and_6 (out_7[7], \Operação [2], ~\Operação [1], \Operação [0]);  // AND_Gate
  and and_7 (out_8[7], \Operação [2], \Operação [1], ~\Operação [0]);  // AND_Gate
  and and_8 (out_9[7], \Operação [2], \Operação [1], \Operação [0]);

  assign out_2[6:0] = {7{out_2[7]}};
  assign out_3[6:0] = {7{out_3[7]}};
  assign out_4[6:0] = {7{out_4[7]}};
  assign out_5[6:0] = {7{out_5[7]}};
  assign out_6[6:0] = {7{out_6[7]}};
  assign out_7[6:0] = {7{out_7[7]}};
  assign out_8[6:0] = {7{out_8[7]}};
  assign out_9[6:0] = {7{out_9[7]}};
endmodule

module Somador_Look_Ahead (
  input  [7:0] A,
  input  in_2,
  input  [7:0] B,
  output [7:0] out_4
);

  wire and_1_out, and_2_out, and_3_out, and_4_out, and_5_out, and_6_out, and_7_out, and_8_out, and_9_out,
       and_10_out, and_11_out, and_12_out, and_13_out, and_14_out, and_15_out, and_16_out, and_17_out,
       and_18_out, and_19_out, and_20_out, and_21_out, and_22_out, and_23_out, and_24_out, and_25_out,
       and_26_out, and_27_out, and_28_out, and_29_out, and_30_out, and_31_out, and_32_out, and_33_out,
       and_34_out, and_35_out, and_36_out, G0___P0_g__a_b, G0___P0_p__a_b, G1___P1_g__a_b, G1___P1_p__a_b,
       G2___P2_g__a_b, G2___P2_p__a_b, G3___P3_g__a_b, G3___P3_p__a_b, G4___P4_g__a_b, G4___P4_p__a_b,
       G5___P5_g__a_b, G5___P5_p__a_b, G6___P6_g__a_b, G6___P6_p__a_b, G7___P7_g__a_b, G7___P7_p__a_b,
       or_1_out, or_2_out, or_3_out, or_4_out, or_5_out, or_6_out, or_7_out, or_8_out;
  wire [7:0] xor_1_out;

  // Probe on out_4
  // Probe on A
  // Probe on xor_1_out
  assign xor_1_out = B ^ {8{in_2}};  // XOR_Gate xor_1, 8 bits wide
  GePeto G0___P0 (.G__A_B(G0___P0_g__a_b), .P__A_B(G0___P0_p__a_b), .A(A[0]), .B(xor_1_out[0]));
  GePeto G1___P1 (.G__A_B(G1___P1_g__a_b), .P__A_B(G1___P1_p__a_b), .A(A[1]), .B(xor_1_out[1]));
  GePeto G2___P2 (.G__A_B(G2___P2_g__a_b), .P__A_B(G2___P2_p__a_b), .A(A[2]), .B(xor_1_out[2]));
  GePeto G3___P3 (.G__A_B(G3___P3_g__a_b), .P__A_B(G3___P3_p__a_b), .A(A[3]), .B(xor_1_out[3]));
  GePeto G4___P4 (.G__A_B(G4___P4_g__a_b), .P__A_B(G4___P4_p__a_b), .A(A[4]), .B(xor_1_out[4]));
  GePeto G5___P5 (.G__A_B(G5___P5_g__a_b), .P__A_B(G5___P5_p__a_b), .A(A[5]), .B(xor_1_out[5]));
  GePeto G6___P6 (.G__A_B(G6___P6_g__a_b), .P__A_B(G6___P6_p__a_b), .A(A[6]), .B(xor_1_out[6]));
  GePeto G7___P7 (.G__A_B(G7___P7_g__a_b), .P__A_B(G7___P7_p__a_b), .A(A[7]), .B(xor_1_out[7]));
  and and_1 (and_1_out, G7___P7_p__a_b, G6___P6_g__a_b);
  and and_2 (and_2_out, G7___P7_p__a_b, G6___P6_p__a_b, G5___P5_g__a_b);
  or or_1 (or_1_out, G7___P7_g__a_b, and_1_out, and_2_out, and_3_out, and_4_out, and_5_out, and_6_out, and_7_out, and_8_out);
  LED Overflow (.in(or_1_out));
  and and_3 (and_3_out, G7___P7_p__a_b, G6___P6_p__a_b, G5___P5_p__a_b, G4___P4_g__a_b);
  and and_4 (and_4_out, G7___P7_p__a_b, G6___P6_p__a_b, G5___P5_p__a_b, G4___P4_p__a_b, G3___P3_g__a_b);
  and and_5 (and_5_out, G7___P7_p__a_b, G6___P6_p__a_b, G5___P5_p__a_b, G4___P4_p__a_b, G3___P3_p__a_b, G2___P2_g__a_b);
  and and_6 (and_6_out, G7___P7_p__a_b, G6___P6_p__a_b, G5___P5_p__a_b, G4___P4_p__a_b, G3___P3_p__a_b, G2___P2_p__a_b, G1___P1_g__a_b);
  and and_7 (and_7_out, G7___P7_p__a_b, G6___P6_p__a_b, G5___P5_p__a_b, G4___P4_p__a_b, G3___P3_p__a_b, G2___P2_p__a_b, G1___P1_p__a_b, G0___P0_g__a_b);
  and and_8 (and_8_out, G7___P7_p__a_b, G6___P6_p__a_b, G5___P5_p__a_b, G4___P4_p__a_b, G3___P3_p__a_b, G2___P2_p__a_b, G1___P1_p__a_b, G0___P0_p__a_b, in_2);
  Somador_de_1_bit somador_de_1_bit_1 (.S(out_4[7]), .A(A[7]), .B(xor_1_out[7]), .C_in(or_2_out));
  and and_9 (and_9_out, G6___P6_p__a_b, G5___P5_p__a_b, G4___P4_g__a_b);
  and and_10 (and_10_out, G6___P6_p__a_b, G5___P5_g__a_b);
  or or_2 (or_2_out, G6___P6_g__a_b, and_10_out, and_9_out, and_11_out, and_12_out, and_13_out, and_14_out, and_15_out);
  and and_11 (and_11_out, G6___P6_p__a_b, G5___P5_p__a_b, G4___P4_p__a_b, G3___P3_g__a_b);
  and and_12 (and_12_out, G6___P6_p__a_b, G5___P5_p__a_b, G4___P4_p__a_b, G3___P3_p__a_b, G2___P2_g__a_b);
  and and_13 (and_13_out, G6___P6_p__a_b, G5___P5_p__a_b, G4___P4_p__a_b, G3___P3_p__a_b, G2___P2_p__a_b, G1___P1_g__a_b);
  and and_14 (and_14_out, G6___P6_p__a_b, G5___P5_p__a_b, G4___P4_p__a_b, G3___P3_p__a_b, G2___P2_p__a_b, G1___P1_p__a_b, G0___P0_g__a_b);
  and and_15 (and_15_out, G6___P6_p__a_b, G5___P5_p__a_b, G4___P4_p__a_b, G3___P3_p__a_b, G2___P2_p__a_b, G1___P1_p__a_b, G0___P0_p__a_b, in_2);
  and and_16 (and_16_out, G5___P5_p__a_b, G4___P4_g__a_b);
  or or_3 (or_3_out, G5___P5_g__a_b, and_16_out, and_17_out, and_18_out, and_19_out, and_20_out, and_21_out);
  Somador_de_1_bit somador_de_1_bit_2 (.S(out_4[6]), .A(A[6]), .B(xor_1_out[6]), .C_in(or_3_out));
  and and_17 (and_17_out, G5___P5_p__a_b, G4___P4_p__a_b, G3___P3_g__a_b);
  and and_18 (and_18_out, G5___P5_p__a_b, G4___P4_p__a_b, G3___P3_p__a_b, G2___P2_g__a_b);
  and and_19 (and_19_out, G5___P5_p__a_b, G4___P4_p__a_b, G3___P3_p__a_b, G2___P2_p__a_b, G1___P1_g__a_b);
  and and_20 (and_20_out, G5___P5_p__a_b, G4___P4_p__a_b, G3___P3_p__a_b, G2___P2_p__a_b, G1___P1_p__a_b, G0___P0_g__a_b);
  and and_21 (and_21_out, G5___P5_p__a_b, G4___P4_p__a_b, G3___P3_p__a_b, G2___P2_p__a_b, G1___P1_p__a_b, G0___P0_p__a_b, in_2);
  Somador_de_1_bit somador_de_1_bit_3 (.S(out_4[5]), .A(A[5]), .B(xor_1_out[5]), .C_in(or_4_out));
  and and_22 (and_22_out, G4___P4_p__a_b, G3___P3_g__a_b);
  and and_23 (and_23_out, G4___P4_p__a_b, G3___P3_p__a_b, G2___P2_g__a_b);
  or or_4 (or_4_out, G4___P4_g__a_b, and_22_out, and_23_out, and_24_out, and_25_out, and_26_out);
  and and_24 (and_24_out, G4___P4_p__a_b, G3___P3_p__a_b, G2___P2_p__a_b, G1___P1_g__a_b);
  and and_25 (and_25_out, G4___P4_p__a_b, G3___P3_p__a_b, G2___P2_p__a_b, G1___P1_p__a_b, G0___P0_g__a_b);
  and and_26 (and_26_out, G4___P4_p__a_b, G3___P3_p__a_b, G2___P2_p__a_b, G1___P1_p__a_b, G0___P0_p__a_b, in_2);
  Somador_de_1_bit somador_de_1_bit_4 (.S(out_4[4]), .A(A[4]), .B(xor_1_out[4]), .C_in(or_5_out));
  and and_27 (and_27_out, G3___P3_p__a_b, G2___P2_g__a_b);
  and and_28 (and_28_out, G3___P3_p__a_b, G2___P2_p__a_b, G1___P1_g__a_b);
  or or_5 (or_5_out, G3___P3_g__a_b, and_27_out, and_28_out, and_29_out, and_30_out);
  and and_29 (and_29_out, G3___P3_p__a_b, G2___P2_p__a_b, G1___P1_p__a_b, G0___P0_g__a_b);
  and and_30 (and_30_out, G3___P3_p__a_b, G2___P2_p__a_b, G1___P1_p__a_b, G0___P0_p__a_b, in_2);
  Somador_de_1_bit somador_de_1_bit_5 (.S(out_4[3]), .A(A[3]), .B(xor_1_out[3]), .C_in(or_6_out));
  and and_31 (and_31_out, G2___P2_p__a_b, G1___P1_g__a_b);
  and and_32 (and_32_out, G2___P2_p__a_b, G1___P1_p__a_b, G0___P0_g__a_b);
  or or_6 (or_6_out, G2___P2_g__a_b, and_31_out, and_32_out, and_33_out);
  and and_33 (and_33_out, G2___P2_p__a_b, G1___P1_p__a_b, G0___P0_p__a_b, in_2);
  Somador_de_1_bit somador_de_1_bit_6 (.S(out_4[2]), .A(A[2]), .B(xor_1_out[2]), .C_in(or_7_out));
  and and_34 (and_34_out, G1___P1_p__a_b, G0___P0_g__a_b);
  and and_35 (and_35_out, G1___P1_p__a_b, G0___P0_p__a_b, in_2);
  or or_7 (or_7_out, G1___P1_g__a_b, and_34_out, and_35_out);
  and and_36 (and_36_out, G0___P0_p__a_b, in_2);
  or or_8 (or_8_out, G0___P0_g__a_b, and_36_out);
  Somador_de_1_bit somador_de_1_bit_7 (.S(out_4[1]), .A(A[1]), .B(xor_1_out[1]), .C_in(or_8_out));
  Somador_de_1_bit somador_de_1_bit_8 (.S(out_4[0]), .A(A[0]), .B(xor_1_out[0]), .C_in(in_2));
endmodule

module Somador_de_1_bit (
  input  A,
  input  B,
  input  C_in,
  output S
);

  wire xor_1_out;

  xor xor_1 (xor_1_out, B, C_in);
  xor xor_2 (S, A, xor_1_out);
endmodule

module GePeto (
  input  A,
  input  B,
  output G__A_B,
  output P__A_B
);

  and and_1 (G__A_B, A, B);
  or or_1 (P__A_B, A, B);
endmodule

module ULA (
  input  [7:0] A,
  input  [7:0] B,
  input  [2:0] Op,
  output [7:0] out_4
);

  wire [7:0] and_1_out, and_2_out, and_3_out, and_4_out, and_5_out, and_6_out, and_7_out, and_8_out,
       divider_1_out, divider_1_rem, multiplier_1_out, operador_1_out_2, operador_1_out_3, operador_1_out_4,
       operador_1_out_5, operador_1_out_6, operador_1_out_7, operador_1_out_8, operador_1_out_9, or_1_out,
       or_3_out, somador_look_ahead_1_out_4, xor_1_out;

  // Probe on A
  // Probe on B
  Operador operador_1 (
    .\Operação (Op), .out_2(operador_1_out_2), .out_3(operador_1_out_3), .out_4(operador_1_out_4),
    .out_5(operador_1_out_5), .out_6(operador_1_out_6), .out_7(operador_1_out_7), .out_8(operador_1_out_8),
    .out_9(operador_1_out_9));
  assign and_1_out = operador_1_out_2 & or_1_out;  // AND_Gate and_1, 8 bits wide
  assign or_1_out = A | B;  // OR_Gate or_1, 8 bits wide
  assign and_2_out = A & B;  // AND_Gate and_2, 8 bits wide
  assign and_3_out = operador_1_out_3 & and_2_out;  // AND_Gate and_3, 8 bits wide
  assign out_4 = and_1_out | and_3_out | and_4_out | and_5_out | and_6_out | and_7_out | and_8_out;  // OR_Gate or_2, 8 bits wide
  // Probe on out_4
  assign xor_1_out = A ^ B;  // XOR_Gate xor_1, 8 bits wide
  assign and_4_out = operador_1_out_4 & xor_1_out;  // AND_Gate and_4, 8 bits wide
  assign or_3_out = operador_1_out_5 | operador_1_out_6;  // OR_Gate or_3, 8 bits wide
  Somador_Look_Ahead somador_look_ahead_1 (
    .A(A), .B(B), .in_2(operador_1_out_6[0]), .out_4(somador_look_ahead_1_out_4));
  assign and_5_out = or_3_out & somador_look_ahead_1_out_4;  // AND_Gate and_5, 8 bits wide
  Multiplier multiplier_1 (.a(A), .b(B), .out(multiplier_1_out));  // open: cin, cout
  assign and_6_out = operador_1_out_7 & multiplier_1_out;  // AND_Gate and_6, 8 bits wide
  Divider divider_1 (.a(A), .b(B), .out(divider_1_out), .rem(divider_1_rem));  // open: upper
  assign and_7_out = operador_1_out_8 & divider_1_out;  // AND_Gate and_7, 8 bits wide
  assign and_8_out = operador_1_out_9 & divider_1_rem;  // AND_Gate and_8, 8 bits wide

  // Notes on the sheet:
  //   000 - OR
  //   001 - AND
  //   010 - XOR
  //   011 - SOMA
  //   100 - SUBTRAÇÃO
  //   110 - DIVISÃO
  //   111 - RESTO
  //   101 - MULTIPLICAÇÃO
endmodule

module Registrador_8bits (
  input  [7:0] Entrada,
  input  Leitura_escrita,
  output [7:0] \Saída 
);

  D_Flip_Flop d_ff_1 (.clk(Leitura_escrita), .D(Entrada[7]), .Q(\Saída [7]));  // open: Qn, preset, en, reset
  D_Flip_Flop d_ff_2 (.clk(Leitura_escrita), .D(Entrada[6]), .Q(\Saída [6]));  // open: Qn, preset, en, reset
  D_Flip_Flop d_ff_3 (.clk(Leitura_escrita), .D(Entrada[5]), .Q(\Saída [5]));  // open: Qn, preset, en, reset
  D_Flip_Flop d_ff_4 (.clk(Leitura_escrita), .D(Entrada[4]), .Q(\Saída [4]));  // open: Qn, preset, en, reset
  D_Flip_Flop d_ff_5 (.clk(Leitura_escrita), .D(Entrada[3]), .Q(\Saída [3]));  // open: Qn, preset, en, reset
  D_Flip_Flop d_ff_6 (.clk(Leitura_escrita), .D(Entrada[2]), .Q(\Saída [2]));  // open: Qn, preset, en, reset
  D_Flip_Flop d_ff_7 (.clk(Leitura_escrita), .D(Entrada[1]), .Q(\Saída [1]));  // open: Qn, preset, en, reset
  D_Flip_Flop d_ff_8 (.clk(Leitura_escrita), .D(Entrada[0]), .Q(\Saída [0]));  // open: Qn, preset, en, reset
endmodule

module contador0a7 (
  input  Clock,
  output [2:0] \Saída 
);

  T_Flip_Flop #(.trigger("falling")) t_ff_1 (.clk(Clock), .T(1'b1), .Q(\Saída [0]));  // open: Qn, preset, reset, en
  T_Flip_Flop #(.trigger("falling")) t_ff_2 (
    .clk(\Saída [0]), .T(1'b1), .Q(\Saída [1]));  // open: Qn, preset, reset, en
  T_Flip_Flop #(.trigger("falling")) t_ff_3 (
    .clk(\Saída [1]), .T(1'b1), .Q(\Saída [2]));  // open: Qn, preset, reset, en
endmodule

module Memoria_11x8 (
  input  [10:0] Entrada,
  input  [2:0] \Endereço ,
  input  Leitura_Escrita,
  output [10:0] \Saída 
);

  wire and_1_out, and_2_out, and_3_out, and_4_out, and_5_out, and_6_out, and_7_out, and_8_out, and_9_out,
       and_10_out, and_11_out, and_12_out, and_13_out, and_14_out, and_15_out, and_16_out, and_17_out,
       and_18_out, and_19_out, and_20_out, and_21_out, and_22_out, and_23_out, and_24_out, and_25_out,
       and_26_out, and_27_out, and_28_out, and_29_out, and_30_out, and_31_out, and_32_out, and_33_out,
       and_34_out, and_35_out, and_36_out, and_37_out, and_38_out, and_39_out, and_40_out, and_41_out,
       and_42_out, and_43_out, and_44_out, and_45_out, and_46_out, and_47_out, and_48_out, and_49_out,
       and_50_out, and_51_out, and_52_out, and_53_out, and_54_out, and_55_out, and_56_out, and_57_out,
       and_58_out, and_59_out, and_60_out, and_61_out, and_62_out, and_63_out, and_64_out, and_65_out,
       and_66_out, and_67_out, and_68_out, and_69_out, and_70_out, and_71_out, and_72_out, and_73_out,
       and_74_out, and_75_out, and_76_out, and_77_out, and_78_out, and_79_out, and_80_out, and_81_out,
       and_82_out, and_83_out, and_84_out, and_85_out, and_86_out, and_87_out, and_88_out, and_89_out,
       and_90_out, and_91_out, and_92_out, and_93_out, and_94_out, and_95_out, and_96_out, and_97_out,
       and_98_out, and_99_out, and_100_out, and_101_out, and_102_out, and_103_out, and_104_out, d_ff_1_q,
       d_ff_2_q, d_ff_3_q, d_ff_4_q, d_ff_5_q, d_ff_6_q, d_ff_7_q, d_ff_8_q, d_ff_9_q, d_ff_10_q, d_ff_11_q,
       d_ff_12_q, d_ff_13_q, d_ff_14_q, d_ff_15_q, d_ff_16_q, d_ff_17_q, d_ff_18_q, d_ff_19_q, d_ff_20_q,
       d_ff_21_q, d_ff_22_q, d_ff_23_q, d_ff_24_q, d_ff_25_q, d_ff_26_q, d_ff_27_q, d_ff_28_q, d_ff_29_q,
       d_ff_30_q, d_ff_31_q, d_ff_32_q, d_ff_33_q, d_ff_34_q, d_ff_35_q, d_ff_36_q, d_ff_37_q, d_ff_38_q,
       d_ff_39_q, d_ff_40_q, d_ff_41_q, d_ff_42_q, d_ff_43_q, d_ff_44_q, d_ff_45_q, d_ff_46_q, d_ff_47_q,
       d_ff_48_q, d_ff_49_q, d_ff_50_q, d_ff_51_q, d_ff_52_q, d_ff_53_q, d_ff_54_q, d_ff_55_q, d_ff_56_q,
       d_ff_57_q, d_ff_58_q, d_ff_59_q, d_ff_60_q, d_ff_61_q, d_ff_62_q, d_ff_63_q, d_ff_64_q, d_ff_65_q,
       d_ff_66_q, d_ff_67_q, d_ff_68_q, d_ff_69_q, d_ff_70_q, d_ff_71_q, d_ff_72_q, d_ff_73_q, d_ff_74_q,
       d_ff_75_q, d_ff_76_q, d_ff_77_q, d_ff_78_q, d_ff_79_q, d_ff_80_q, d_ff_81_q, d_ff_82_q, d_ff_83_q,
       d_ff_84_q, d_ff_85_q, d_ff_86_q, d_ff_87_q, d_ff_88_q;

  and and_1 (and_1_out, ~\Endereço [2], ~\Endereço [1], ~\Endereço [0]);  // AND_Gate
  and and_2 (and_2_out, ~\Endereço [2], ~\Endereço [1], \Endereço [0]);  // AND_Gate
  and and_3 (and_3_out, ~\Endereço [2], \Endereço [1], ~\Endereço [0]);  // AND_Gate
  and and_4 (and_4_out, ~\Endereço [2], \Endereço [1], \Endereço [0]);  // AND_Gate
  and and_5 (and_5_out, \Endereço [2], ~\Endereço [1], ~\Endereço [0]);  // AND_Gate
  and and_6 (and_6_out, \Endereço [2], ~\Endereço [1], \Endereço [0]);  // AND_Gate
  and and_7 (and_7_out, \Endereço [2], \Endereço [1], ~\Endereço [0]);  // AND_Gate
  and and_8 (and_8_out, \Endereço [2], \Endereço [1], \Endereço [0]);
  and and_9 (and_9_out, and_1_out, Leitura_Escrita);
  and and_10 (and_10_out, and_2_out, Leitura_Escrita);
  and and_11 (and_11_out, and_3_out, Leitura_Escrita);
  and and_12 (and_12_out, and_4_out, Leitura_Escrita);
  and and_13 (and_13_out, and_5_out, Leitura_Escrita);
  and and_14 (and_14_out, and_6_out, Leitura_Escrita);
  and and_15 (and_15_out, and_7_out, Leitura_Escrita);
  and and_16 (and_16_out, and_8_out, Leitura_Escrita);
  D_Flip_Flop #(.trigger("falling")) d_ff_1 (
    .clk(and_9_out), .D(Entrada[10]), .Q(d_ff_1_q));  // open: Qn, preset, en, reset
  and and_17 (and_17_out, d_ff_1_q, and_1_out);
  D_Flip_Flop #(.trigger("falling")) d_ff_2 (
    .clk(and_10_out), .D(Entrada[10]), .Q(d_ff_2_q));  // open: Qn, preset, en, reset
  and and_18 (and_18_out, d_ff_2_q, and_2_out);
  D_Flip_Flop #(.trigger("falling")) d_ff_3 (
    .clk(and_11_out), .D(Entrada[10]), .Q(d_ff_3_q));  // open: Qn, preset, en, reset
  and and_19 (and_19_out, d_ff_3_q, and_3_out);
  D_Flip_Flop #(.trigger("falling")) d_ff_4 (
    .clk(and_12_out), .D(Entrada[10]), .Q(d_ff_4_q));  // open: Qn, preset, en, reset
  and and_20 (and_20_out, d_ff_4_q, and_4_out);
  D_Flip_Flop #(.trigger("falling")) d_ff_5 (
    .clk(and_13_out), .D(Entrada[10]), .Q(d_ff_5_q));  // open: Qn, preset, en, reset
  and and_21 (and_21_out, d_ff_5_q, and_5_out);
  D_Flip_Flop #(.trigger("falling")) d_ff_6 (
    .clk(and_14_out), .D(Entrada[10]), .Q(d_ff_6_q));  // open: Qn, preset, en, reset
  and and_22 (and_22_out, d_ff_6_q, and_6_out);
  D_Flip_Flop #(.trigger("falling")) d_ff_7 (
    .clk(and_15_out), .D(Entrada[10]), .Q(d_ff_7_q));  // open: Qn, preset, en, reset
  and and_23 (and_23_out, d_ff_7_q, and_7_out);
  D_Flip_Flop #(.trigger("falling")) d_ff_8 (
    .clk(and_16_out), .D(Entrada[10]), .Q(d_ff_8_q));  // open: Qn, preset, en, reset
  and and_24 (and_24_out, d_ff_8_q, and_8_out);
  or or_1 (\Saída [10], and_24_out, and_23_out, and_22_out, and_21_out, and_20_out, and_19_out, and_18_out, and_17_out);
  D_Flip_Flop #(.trigger("falling")) d_ff_9 (
    .clk(and_9_out), .D(Entrada[9]), .Q(d_ff_9_q));  // open: Qn, preset, en, reset
  and and_25 (and_25_out, d_ff_9_q, and_1_out);
  D_Flip_Flop #(.trigger("falling")) d_ff_10 (
    .clk(and_10_out), .D(Entrada[9]), .Q(d_ff_10_q));  // open: Qn, preset, en, reset
  and and_26 (and_26_out, d_ff_10_q, and_2_out);
  D_Flip_Flop #(.trigger("falling")) d_ff_11 (
    .clk(and_11_out), .D(Entrada[9]), .Q(d_ff_11_q));  // open: Qn, preset, en, reset
  and and_27 (and_27_out, d_ff_11_q, and_3_out);
  D_Flip_Flop #(.trigger("falling")) d_ff_12 (
    .clk(and_12_out), .D(Entrada[9]), .Q(d_ff_12_q));  // open: Qn, preset, en, reset
  and and_28 (and_28_out, d_ff_12_q, and_4_out);
  D_Flip_Flop #(.trigger("falling")) d_ff_13 (
    .clk(and_13_out), .D(Entrada[9]), .Q(d_ff_13_q));  // open: Qn, preset, en, reset
  and and_29 (and_29_out, d_ff_13_q, and_5_out);
  D_Flip_Flop #(.trigger("falling")) d_ff_14 (
    .clk(and_14_out), .D(Entrada[9]), .Q(d_ff_14_q));  // open: Qn, preset, en, reset
  and and_30 (and_30_out, d_ff_14_q, and_6_out);
  D_Flip_Flop #(.trigger("falling")) d_ff_15 (
    .clk(and_15_out), .D(Entrada[9]), .Q(d_ff_15_q));  // open: Qn, preset, en, reset
  and and_31 (and_31_out, d_ff_15_q, and_7_out);
  D_Flip_Flop #(.trigger("falling")) d_ff_16 (
    .clk(and_16_out), .D(Entrada[9]), .Q(d_ff_16_q));  // open: Qn, preset, en, reset
  and and_32 (and_32_out, d_ff_16_q, and_8_out);
  or or_2 (\Saída [9], and_32_out, and_31_out, and_30_out, and_29_out, and_28_out, and_27_out, and_26_out, and_25_out);
  D_Flip_Flop #(.trigger("falling")) d_ff_17 (
    .clk(and_9_out), .D(Entrada[8]), .Q(d_ff_17_q));  // open: Qn, preset, en, reset
  D_Flip_Flop #(.trigger("falling")) d_ff_18 (
    .clk(and_10_out), .D(Entrada[8]), .Q(d_ff_18_q));  // open: Qn, preset, en, reset
  D_Flip_Flop #(.trigger("falling")) d_ff_19 (
    .clk(and_11_out), .D(Entrada[8]), .Q(d_ff_19_q));  // open: Qn, preset, en, reset
  D_Flip_Flop #(.trigger("falling")) d_ff_20 (
    .clk(and_12_out), .D(Entrada[8]), .Q(d_ff_20_q));  // open: Qn, preset, en, reset
  D_Flip_Flop #(.trigger("falling")) d_ff_21 (
    .clk(and_13_out), .D(Entrada[8]), .Q(d_ff_21_q));  // open: Qn, preset, en, reset
  D_Flip_Flop #(.trigger("falling")) d_ff_22 (
    .clk(and_14_out), .D(Entrada[8]), .Q(d_ff_22_q));  // open: Qn, preset, en, reset
  D_Flip_Flop #(.trigger("falling")) d_ff_23 (
    .clk(and_15_out), .D(Entrada[8]), .Q(d_ff_23_q));  // open: Qn, preset, en, reset
  D_Flip_Flop #(.trigger("falling")) d_ff_24 (
    .clk(and_16_out), .D(Entrada[8]), .Q(d_ff_24_q));  // open: Qn, preset, en, reset
  and and_33 (and_33_out, d_ff_17_q, and_1_out);
  and and_34 (and_34_out, d_ff_18_q, and_2_out);
  and and_35 (and_35_out, d_ff_19_q, and_3_out);
  and and_36 (and_36_out, d_ff_20_q, and_4_out);
  and and_37 (and_37_out, d_ff_21_q, and_5_out);
  and and_38 (and_38_out, d_ff_22_q, and_6_out);
  and and_39 (and_39_out, d_ff_23_q, and_7_out);
  and and_40 (and_40_out, d_ff_24_q, and_8_out);
  or or_3 (\Saída [8], and_40_out, and_39_out, and_38_out, and_37_out, and_36_out, and_35_out, and_34_out, and_33_out);
  D_Flip_Flop #(.trigger("falling")) d_ff_25 (
    .clk(and_9_out), .D(Entrada[7]), .Q(d_ff_25_q));  // open: Qn, preset, en, reset
  D_Flip_Flop #(.trigger("falling")) d_ff_26 (
    .clk(and_10_out), .D(Entrada[7]), .Q(d_ff_26_q));  // open: Qn, preset, en, reset
  D_Flip_Flop #(.trigger("falling")) d_ff_27 (
    .clk(and_11_out), .D(Entrada[7]), .Q(d_ff_27_q));  // open: Qn, preset, en, reset
  D_Flip_Flop #(.trigger("falling")) d_ff_28 (
    .clk(and_12_out), .D(Entrada[7]), .Q(d_ff_28_q));  // open: Qn, preset, en, reset
  D_Flip_Flop #(.trigger("falling")) d_ff_29 (
    .clk(and_13_out), .D(Entrada[7]), .Q(d_ff_29_q));  // open: Qn, preset, en, reset
  D_Flip_Flop #(.trigger("falling")) d_ff_30 (
    .clk(and_14_out), .D(Entrada[7]), .Q(d_ff_30_q));  // open: Qn, preset, en, reset
  D_Flip_Flop #(.trigger("falling")) d_ff_31 (
    .clk(and_15_out), .D(Entrada[7]), .Q(d_ff_31_q));  // open: Qn, preset, en, reset
  D_Flip_Flop #(.trigger("falling")) d_ff_32 (
    .clk(and_16_out), .D(Entrada[7]), .Q(d_ff_32_q));  // open: Qn, preset, en, reset
  and and_41 (and_41_out, d_ff_25_q, and_1_out);
  and and_42 (and_42_out, d_ff_26_q, and_2_out);
  and and_43 (and_43_out, d_ff_27_q, and_3_out);
  and and_44 (and_44_out, d_ff_28_q, and_4_out);
  and and_45 (and_45_out, d_ff_29_q, and_5_out);
  and and_46 (and_46_out, d_ff_30_q, and_6_out);
  and and_47 (and_47_out, d_ff_31_q, and_7_out);
  and and_48 (and_48_out, d_ff_32_q, and_8_out);
  or or_4 (\Saída [7], and_48_out, and_47_out, and_46_out, and_45_out, and_44_out, and_43_out, and_42_out, and_41_out);
  D_Flip_Flop #(.trigger("falling")) d_ff_33 (
    .clk(and_9_out), .D(Entrada[6]), .Q(d_ff_33_q));  // open: Qn, preset, en, reset
  and and_49 (and_49_out, d_ff_33_q, and_1_out);
  D_Flip_Flop #(.trigger("falling")) d_ff_34 (
    .clk(and_10_out), .D(Entrada[6]), .Q(d_ff_34_q));  // open: Qn, preset, en, reset
  and and_50 (and_50_out, d_ff_34_q, and_2_out);
  D_Flip_Flop #(.trigger("falling")) d_ff_35 (
    .clk(and_11_out), .D(Entrada[6]), .Q(d_ff_35_q));  // open: Qn, preset, en, reset
  and and_51 (and_51_out, d_ff_35_q, and_3_out);
  D_Flip_Flop #(.trigger("falling")) d_ff_36 (
    .clk(and_12_out), .D(Entrada[6]), .Q(d_ff_36_q));  // open: Qn, preset, en, reset
  and and_52 (and_52_out, d_ff_36_q, and_4_out);
  D_Flip_Flop #(.trigger("falling")) d_ff_37 (
    .clk(and_13_out), .D(Entrada[6]), .Q(d_ff_37_q));  // open: Qn, preset, en, reset
  and and_53 (and_53_out, d_ff_37_q, and_5_out);
  D_Flip_Flop #(.trigger("falling")) d_ff_38 (
    .clk(and_14_out), .D(Entrada[6]), .Q(d_ff_38_q));  // open: Qn, preset, en, reset
  and and_54 (and_54_out, d_ff_38_q, and_6_out);
  D_Flip_Flop #(.trigger("falling")) d_ff_39 (
    .clk(and_15_out), .D(Entrada[6]), .Q(d_ff_39_q));  // open: Qn, preset, en, reset
  and and_55 (and_55_out, d_ff_39_q, and_7_out);
  D_Flip_Flop #(.trigger("falling")) d_ff_40 (
    .clk(and_16_out), .D(Entrada[6]), .Q(d_ff_40_q));  // open: Qn, preset, en, reset
  and and_56 (and_56_out, d_ff_40_q, and_8_out);
  or or_5 (\Saída [6], and_56_out, and_55_out, and_54_out, and_53_out, and_52_out, and_51_out, and_50_out, and_49_out);
  D_Flip_Flop #(.trigger("falling")) d_ff_41 (
    .clk(and_9_out), .D(Entrada[5]), .Q(d_ff_41_q));  // open: Qn, preset, en, reset
  and and_57 (and_57_out, d_ff_41_q, and_1_out);
  D_Flip_Flop #(.trigger("falling")) d_ff_42 (
    .clk(and_10_out), .D(Entrada[5]), .Q(d_ff_42_q));  // open: Qn, preset, en, reset
  and and_58 (and_58_out, d_ff_42_q, and_2_out);
  D_Flip_Flop #(.trigger("falling")) d_ff_43 (
    .clk(and_11_out), .D(Entrada[5]), .Q(d_ff_43_q));  // open: Qn, preset, en, reset
  and and_59 (and_59_out, d_ff_43_q, and_3_out);
  D_Flip_Flop #(.trigger("falling")) d_ff_44 (
    .clk(and_12_out), .D(Entrada[5]), .Q(d_ff_44_q));  // open: Qn, preset, en, reset
  and and_60 (and_60_out, d_ff_44_q, and_4_out);
  D_Flip_Flop #(.trigger("falling")) d_ff_45 (
    .clk(and_13_out), .D(Entrada[5]), .Q(d_ff_45_q));  // open: Qn, preset, en, reset
  and and_61 (and_61_out, d_ff_45_q, and_5_out);
  D_Flip_Flop #(.trigger("falling")) d_ff_46 (
    .clk(and_14_out), .D(Entrada[5]), .Q(d_ff_46_q));  // open: Qn, preset, en, reset
  and and_62 (and_62_out, d_ff_46_q, and_6_out);
  D_Flip_Flop #(.trigger("falling")) d_ff_47 (
    .clk(and_15_out), .D(Entrada[5]), .Q(d_ff_47_q));  // open: Qn, preset, en, reset
  and and_63 (and_63_out, d_ff_47_q, and_7_out);
  D_Flip_Flop #(.trigger("falling")) d_ff_48 (
    .clk(and_16_out), .D(Entrada[5]), .Q(d_ff_48_q));  // open: Qn, preset, en, reset
  and and_64 (and_64_out, d_ff_48_q, and_8_out);
  or or_6 (\Saída [5], and_64_out, and_63_out, and_62_out, and_61_out, and_60_out, and_59_out, and_58_out, and_57_out);
  D_Flip_Flop #(.trigger("falling")) d_ff_49 (
    .clk(and_9_out), .D(Entrada[4]), .Q(d_ff_49_q));  // open: Qn, preset, en, reset
  D_Flip_Flop #(.trigger("falling")) d_ff_50 (
    .clk(and_10_out), .D(Entrada[4]), .Q(d_ff_50_q));  // open: Qn, preset, en, reset
  D_Flip_Flop #(.trigger("falling")) d_ff_51 (
    .clk(and_11_out), .D(Entrada[4]), .Q(d_ff_51_q));  // open: Qn, preset, en, reset
  D_Flip_Flop #(.trigger("falling")) d_ff_52 (
    .clk(and_12_out), .D(Entrada[4]), .Q(d_ff_52_q));  // open: Qn, preset, en, reset
  D_Flip_Flop #(.trigger("falling")) d_ff_53 (
    .clk(and_13_out), .D(Entrada[4]), .Q(d_ff_53_q));  // open: Qn, preset, en, reset
  D_Flip_Flop #(.trigger("falling")) d_ff_54 (
    .clk(and_14_out), .D(Entrada[4]), .Q(d_ff_54_q));  // open: Qn, preset, en, reset
  D_Flip_Flop #(.trigger("falling")) d_ff_55 (
    .clk(and_15_out), .D(Entrada[4]), .Q(d_ff_55_q));  // open: Qn, preset, en, reset
  D_Flip_Flop #(.trigger("falling")) d_ff_56 (
    .clk(and_16_out), .D(Entrada[4]), .Q(d_ff_56_q));  // open: Qn, preset, en, reset
  and and_65 (and_65_out, d_ff_49_q, and_1_out);
  and and_66 (and_66_out, d_ff_50_q, and_2_out);
  and and_67 (and_67_out, d_ff_51_q, and_3_out);
  and and_68 (and_68_out, d_ff_52_q, and_4_out);
  and and_69 (and_69_out, d_ff_53_q, and_5_out);
  and and_70 (and_70_out, d_ff_54_q, and_6_out);
  and and_71 (and_71_out, d_ff_55_q, and_7_out);
  and and_72 (and_72_out, d_ff_56_q, and_8_out);
  or or_7 (\Saída [4], and_72_out, and_71_out, and_70_out, and_69_out, and_68_out, and_67_out, and_66_out, and_65_out);
  D_Flip_Flop #(.trigger("falling")) d_ff_57 (
    .clk(and_9_out), .D(Entrada[3]), .Q(d_ff_57_q));  // open: Qn, preset, en, reset
  D_Flip_Flop #(.trigger("falling")) d_ff_58 (
    .clk(and_10_out), .D(Entrada[3]), .Q(d_ff_58_q));  // open: Qn, preset, en, reset
  D_Flip_Flop #(.trigger("falling")) d_ff_59 (
    .clk(and_11_out), .D(Entrada[3]), .Q(d_ff_59_q));  // open: Qn, preset, en, reset
  D_Flip_Flop #(.trigger("falling")) d_ff_60 (
    .clk(and_12_out), .D(Entrada[3]), .Q(d_ff_60_q));  // open: Qn, preset, en, reset
  D_Flip_Flop #(.trigger("falling")) d_ff_61 (
    .clk(and_13_out), .D(Entrada[3]), .Q(d_ff_61_q));  // open: Qn, preset, en, reset
  D_Flip_Flop #(.trigger("falling")) d_ff_62 (
    .clk(and_14_out), .D(Entrada[3]), .Q(d_ff_62_q));  // open: Qn, preset, en, reset
  D_Flip_Flop #(.trigger("falling")) d_ff_63 (
    .clk(and_15_out), .D(Entrada[3]), .Q(d_ff_63_q));  // open: Qn, preset, en, reset
  D_Flip_Flop #(.trigger("falling")) d_ff_64 (
    .clk(and_16_out), .D(Entrada[3]), .Q(d_ff_64_q));  // open: Qn, preset, en, reset
  and and_73 (and_73_out, d_ff_57_q, and_1_out);
  and and_74 (and_74_out, d_ff_58_q, and_2_out);
  and and_75 (and_75_out, d_ff_59_q, and_3_out);
  and and_76 (and_76_out, d_ff_60_q, and_4_out);
  and and_77 (and_77_out, d_ff_61_q, and_5_out);
  and and_78 (and_78_out, d_ff_62_q, and_6_out);
  and and_79 (and_79_out, d_ff_63_q, and_7_out);
  and and_80 (and_80_out, d_ff_64_q, and_8_out);
  or or_8 (\Saída [3], and_80_out, and_79_out, and_78_out, and_77_out, and_76_out, and_75_out, and_74_out, and_73_out);
  D_Flip_Flop #(.trigger("falling")) d_ff_65 (
    .clk(and_9_out), .D(Entrada[2]), .Q(d_ff_65_q));  // open: Qn, preset, en, reset
  and and_81 (and_81_out, d_ff_65_q, and_1_out);
  D_Flip_Flop #(.trigger("falling")) d_ff_66 (
    .clk(and_10_out), .D(Entrada[2]), .Q(d_ff_66_q));  // open: Qn, preset, en, reset
  and and_82 (and_82_out, d_ff_66_q, and_2_out);
  D_Flip_Flop #(.trigger("falling")) d_ff_67 (
    .clk(and_11_out), .D(Entrada[2]), .Q(d_ff_67_q));  // open: Qn, preset, en, reset
  and and_83 (and_83_out, d_ff_67_q, and_3_out);
  D_Flip_Flop #(.trigger("falling")) d_ff_68 (
    .clk(and_12_out), .D(Entrada[2]), .Q(d_ff_68_q));  // open: Qn, preset, en, reset
  and and_84 (and_84_out, d_ff_68_q, and_4_out);
  D_Flip_Flop #(.trigger("falling")) d_ff_69 (
    .clk(and_13_out), .D(Entrada[2]), .Q(d_ff_69_q));  // open: Qn, preset, en, reset
  and and_85 (and_85_out, d_ff_69_q, and_5_out);
  D_Flip_Flop #(.trigger("falling")) d_ff_70 (
    .clk(and_14_out), .D(Entrada[2]), .Q(d_ff_70_q));  // open: Qn, preset, en, reset
  and and_86 (and_86_out, d_ff_70_q, and_6_out);
  D_Flip_Flop #(.trigger("falling")) d_ff_71 (
    .clk(and_15_out), .D(Entrada[2]), .Q(d_ff_71_q));  // open: Qn, preset, en, reset
  and and_87 (and_87_out, d_ff_71_q, and_7_out);
  D_Flip_Flop #(.trigger("falling")) d_ff_72 (
    .clk(and_16_out), .D(Entrada[2]), .Q(d_ff_72_q));  // open: Qn, preset, en, reset
  and and_88 (and_88_out, d_ff_72_q, and_8_out);
  or or_9 (\Saída [2], and_88_out, and_87_out, and_86_out, and_85_out, and_84_out, and_83_out, and_82_out, and_81_out);
  D_Flip_Flop #(.trigger("falling")) d_ff_73 (
    .clk(and_9_out), .D(Entrada[1]), .Q(d_ff_73_q));  // open: Qn, preset, en, reset
  and and_89 (and_89_out, d_ff_73_q, and_1_out);
  D_Flip_Flop #(.trigger("falling")) d_ff_74 (
    .clk(and_10_out), .D(Entrada[1]), .Q(d_ff_74_q));  // open: Qn, preset, en, reset
  and and_90 (and_90_out, d_ff_74_q, and_2_out);
  D_Flip_Flop #(.trigger("falling")) d_ff_75 (
    .clk(and_11_out), .D(Entrada[1]), .Q(d_ff_75_q));  // open: Qn, preset, en, reset
  and and_91 (and_91_out, d_ff_75_q, and_3_out);
  D_Flip_Flop #(.trigger("falling")) d_ff_76 (
    .clk(and_12_out), .D(Entrada[1]), .Q(d_ff_76_q));  // open: Qn, preset, en, reset
  and and_92 (and_92_out, d_ff_76_q, and_4_out);
  D_Flip_Flop #(.trigger("falling")) d_ff_77 (
    .clk(and_13_out), .D(Entrada[1]), .Q(d_ff_77_q));  // open: Qn, preset, en, reset
  and and_93 (and_93_out, d_ff_77_q, and_5_out);
  D_Flip_Flop #(.trigger("falling")) d_ff_78 (
    .clk(and_14_out), .D(Entrada[1]), .Q(d_ff_78_q));  // open: Qn, preset, en, reset
  and and_94 (and_94_out, d_ff_78_q, and_6_out);
  D_Flip_Flop #(.trigger("falling")) d_ff_79 (
    .clk(and_15_out), .D(Entrada[1]), .Q(d_ff_79_q));  // open: Qn, preset, en, reset
  and and_95 (and_95_out, d_ff_79_q, and_7_out);
  D_Flip_Flop #(.trigger("falling")) d_ff_80 (
    .clk(and_16_out), .D(Entrada[1]), .Q(d_ff_80_q));  // open: Qn, preset, en, reset
  and and_96 (and_96_out, d_ff_80_q, and_8_out);
  or or_10 (\Saída [1], and_96_out, and_95_out, and_94_out, and_93_out, and_92_out, and_91_out, and_90_out, and_89_out);
  D_Flip_Flop #(.trigger("falling")) d_ff_81 (
    .clk(and_9_out), .D(Entrada[0]), .Q(d_ff_81_q));  // open: Qn, preset, en, reset
  D_Flip_Flop #(.trigger("falling")) d_ff_82 (
    .clk(and_10_out), .D(Entrada[0]), .Q(d_ff_82_q));  // open: Qn, preset, en, reset
  D_Flip_Flop #(.trigger("falling")) d_ff_83 (
    .clk(and_11_out), .D(Entrada[0]), .Q(d_ff_83_q));  // open: Qn, preset, en, reset
  D_Flip_Flop #(.trigger("falling")) d_ff_84 (
    .clk(and_12_out), .D(Entrada[0]), .Q(d_ff_84_q));  // open: Qn, preset, en, reset
  D_Flip_Flop #(.trigger("falling")) d_ff_85 (
    .clk(and_13_out), .D(Entrada[0]), .Q(d_ff_85_q));  // open: Qn, preset, en, reset
  D_Flip_Flop #(.trigger("falling")) d_ff_86 (
    .clk(and_14_out), .D(Entrada[0]), .Q(d_ff_86_q));  // open: Qn, preset, en, reset
  D_Flip_Flop #(.trigger("falling")) d_ff_87 (
    .clk(and_15_out), .D(Entrada[0]), .Q(d_ff_87_q));  // open: Qn, preset, en, reset
  D_Flip_Flop #(.trigger("falling")) d_ff_88 (
    .clk(and_16_out), .D(Entrada[0]), .Q(d_ff_88_q));  // open: Qn, preset, en, reset
  and and_97 (and_97_out, d_ff_81_q, and_1_out);
  and and_98 (and_98_out, d_ff_82_q, and_2_out);
  and and_99 (and_99_out, d_ff_83_q, and_3_out);
  and and_100 (and_100_out, d_ff_84_q, and_4_out);
  and and_101 (and_101_out, d_ff_85_q, and_5_out);
  and and_102 (and_102_out, d_ff_86_q, and_6_out);
  and and_103 (and_103_out, d_ff_87_q, and_7_out);
  and and_104 (and_104_out, d_ff_88_q, and_8_out);
  or or_11 (\Saída [0], and_104_out, and_103_out, and_102_out, and_101_out, and_100_out, and_99_out, and_98_out, and_97_out);
endmodule
