// Logisim project Relógio 24 hrs- Tiago Defendi (a2571374) - 2023.circ as structural Verilog: 5 circuits, main circuit main
module main (
);

  wire clock_1_out, contador_0_5_1_out_2, contador_0_5_1_out_3, contador_0_5_1_out_4, contador_0_5_1_out_5,
       contador_0_5_1_out_6, contador_0_5_2_out_2, contador_0_5_2_out_3, contador_0_5_2_out_4,
       contador_0_5_2_out_5, contador_0_5_2_out_6, contador_0_9_1_out_2, contador_0_9_1_out_3,
       contador_0_9_1_out_4, contador_0_9_1_out_5, contador_0_9_1_out_6, contador_0_9_2_out_2,
       contador_0_9_2_out_3, contador_0_9_2_out_4, contador_0_9_2_out_5, contador_0_9_2_out_6,
       contador_horas_1_out_3, contador_horas_1_out_4, contador_horas_1_out_5, contador_horas_1_out_6,
       contador_horas_1_out_7, contador_horas_1_out_8, contador_horas_1_out_9, contador_horas_1_out_10,
       decodificador_1_a, decodificador_1_b, decodificador_1_c, decodificador_1_d, decodificador_1_e,
       decodificador_1_f, decodificador_1_g, decodificador_2_a, decodificador_2_b, decodificador_2_c,
       decodificador_2_d, decodificador_2_e, decodificador_2_f, decodificador_2_g, decodificador_3_a,
       decodificador_3_b, decodificador_3_c, decodificador_3_d, decodificador_3_e, decodificador_3_f,
       decodificador_3_g, decodificador_4_a, decodificador_4_b, decodificador_4_c, decodificador_4_d,
       decodificador_4_e, decodificador_4_f, decodificador_4_g, decodificador_5_a, decodificador_5_b,
       decodificador_5_c, decodificador_5_d, decodificador_5_e, decodificador_5_f, decodificador_5_g,
       decodificador_6_a, decodificador_6_b, decodificador_6_c, decodificador_6_d, decodificador_6_e,
       decodificador_6_f, decodificador_6_g;

  Contador_Horas contador_horas_1 (
    .in_1(contador_0_5_1_out_2), .out_9(contador_horas_1_out_9), .out_10(contador_horas_1_out_10),
    .out_5(contador_horas_1_out_5), .out_6(contador_horas_1_out_6), .out_7(contador_horas_1_out_7),
    .out_8(contador_horas_1_out_8), .out_3(contador_horas_1_out_3), .out_4(contador_horas_1_out_4));  // open: out_2
  _7_Segment_Display u_7_segment_display_1 (
    .g(decodificador_1_g), .f(decodificador_1_f), .a(decodificador_1_a), .b(decodificador_1_b),
    .e(decodificador_1_e), .d(decodificador_1_d), .c(decodificador_1_c));  // open: dp
  decodificador decodificador_1 (
    .E1(contador_horas_1_out_9), .a(decodificador_1_a), .b(decodificador_1_b), .c(decodificador_1_c),
    .d(decodificador_1_d), .e(decodificador_1_e), .f(decodificador_1_f), .g(decodificador_1_g),
    .E2(contador_horas_1_out_10), .E3(contador_horas_1_out_3), .E4(contador_horas_1_out_4));
  _7_Segment_Display u_7_segment_display_2 (
    .g(decodificador_2_g), .f(decodificador_2_f), .a(decodificador_2_a), .b(decodificador_2_b),
    .e(decodificador_2_e), .d(decodificador_2_d), .c(decodificador_2_c));  // open: dp
  Contador_0____5 contador_0_5_1 (
    .in_1(contador_0_9_1_out_2), .out_3(contador_0_5_1_out_3), .out_4(contador_0_5_1_out_4),
    .out_5(contador_0_5_1_out_5), .out_6(contador_0_5_1_out_6), .out_2(contador_0_5_1_out_2));
  decodificador decodificador_2 (
    .E1(contador_horas_1_out_5), .a(decodificador_2_a), .b(decodificador_2_b), .c(decodificador_2_c),
    .d(decodificador_2_d), .e(decodificador_2_e), .f(decodificador_2_f), .g(decodificador_2_g),
    .E2(contador_horas_1_out_6), .E3(contador_horas_1_out_7), .E4(contador_horas_1_out_8));
  _7_Segment_Display u_7_segment_display_3 (
    .g(decodificador_3_g), .f(decodificador_3_f), .a(decodificador_3_a), .b(decodificador_3_b),
    .e(decodificador_3_e), .d(decodificador_3_d), .c(decodificador_3_c));  // open: dp
  decodificador decodificador_3 (
    .E1(contador_0_5_1_out_6), .a(decodificador_3_a), .b(decodificador_3_b), .c(decodificador_3_c),
    .d(decodificador_3_d), .e(decodificador_3_e), .f(decodificador_3_f), .g(decodificador_3_g),
    .E2(contador_0_5_1_out_3), .E3(contador_0_5_1_out_4), .E4(contador_0_5_1_out_5));
  Contador_0____9 contador_0_9_1 (
    .in_1(contador_0_5_2_out_2), .out_3(contador_0_9_1_out_3), .out_4(contador_0_9_1_out_4),
    .out_5(contador_0_9_1_out_5), .out_6(contador_0_9_1_out_6), .out_2(contador_0_9_1_out_2));
  _7_Segment_Display u_7_segment_display_4 (
    .g(decodificador_4_g), .f(decodificador_4_f), .a(decodificador_4_a), .b(decodificador_4_b),
    .e(decodificador_4_e), .d(decodificador_4_d), .c(decodificador_4_c));  // open: dp
  Contador_0____5 contador_0_5_2 (
    .in_1(contador_0_9_2_out_2), .out_3(contador_0_5_2_out_3), .out_4(contador_0_5_2_out_4),
    .out_5(contador_0_5_2_out_5), .out_6(contador_0_5_2_out_6), .out_2(contador_0_5_2_out_2));
  decodificador decodificador_4 (
    .E1(contador_0_9_1_out_3), .a(decodificador_4_a), .b(decodificador_4_b), .c(decodificador_4_c),
    .d(decodificador_4_d), .e(decodificador_4_e), .f(decodificador_4_f), .g(decodificador_4_g),
    .E2(contador_0_9_1_out_4), .E3(contador_0_9_1_out_5), .E4(contador_0_9_1_out_6));
  _7_Segment_Display u_7_segment_display_5 (
    .g(decodificador_5_g), .f(decodificador_5_f), .a(decodificador_5_a), .b(decodificador_5_b),
    .e(decodificador_5_e), .d(decodificador_5_d), .c(decodificador_5_c));  // open: dp
  decodificador decodificador_5 (
    .E1(contador_0_5_2_out_6), .a(decodificador_5_a), .b(decodificador_5_b), .c(decodificador_5_c),
    .d(decodificador_5_d), .e(decodificador_5_e), .f(decodificador_5_f), .g(decodificador_5_g),
    .E2(contador_0_5_2_out_3), .E3(contador_0_5_2_out_4), .E4(contador_0_5_2_out_5));
  Contador_0____9 contador_0_9_2 (
    .in_1(clock_1_out), .out_3(contador_0_9_2_out_3), .out_4(contador_0_9_2_out_4),
    .out_5(contador_0_9_2_out_5), .out_6(contador_0_9_2_out_6), .out_2(contador_0_9_2_out_2));
  Clock clock_1 (.out(clock_1_out));
  _7_Segment_Display u_7_segment_display_6 (
    .g(decodificador_6_g), .f(decodificador_6_f), .a(decodificador_6_a), .b(decodificador_6_b),
    .e(decodificador_6_e), .d(decodificador_6_d), .c(decodificador_6_c));  // open: dp
  decodificador decodificador_6 (
    .E1(contador_0_9_2_out_3), .a(decodificador_6_a), .b(decodificador_6_b), .c(decodificador_6_c),
    .d(decodificador_6_d), .e(decodificador_6_e), .f(decodificador_6_f), .g(decodificador_6_g),
    .E2(contador_0_9_2_out_4), .E3(contador_0_9_2_out_5), .E4(contador_0_9_2_out_6));
endmodule

module Contador_0____5 (
  input  in_1,
  output out_2,
  output out_3,
  output out_4,
  output out_5,
  output out_6
);

  wire and_1_out;

  T_Flip_Flop #(.trigger("falling")) t_ff_1 (
    .clk(in_1), .T(1'b1), .Q(out_5), .reset(and_1_out));  // open: Qn, preset, en
  T_Flip_Flop #(.trigger("falling")) t_ff_2 (
    .clk(out_5), .T(1'b1), .Q(out_4), .reset(and_1_out));  // open: Qn, preset, en
  T_Flip_Flop #(.trigger("falling")) t_ff_3 (
    .clk(out_4), .T(1'b1), .Q(out_2), .reset(and_1_out));  // open: Qn, preset, en
  and and_1 (and_1_out, out_2, out_4, ~out_5);  // AND_Gate

  assign out_3 = out_2;
  assign out_6 = 1'b0;
endmodule

module Contador_0____9 (
  input  in_1,
  output out_2,
  output out_3,
  output out_4,
  output out_5,
  output out_6
);

  wire and_1_out;

  T_Flip_Flop #(.trigger("falling")) t_ff_1 (
    .clk(in_1), .T(1'b1), .Q(out_6), .reset(and_1_out));  // open: Qn, preset, en
  T_Flip_Flop #(.trigger("falling")) t_ff_2 (
    .clk(out_6), .T(1'b1), .Q(out_5), .reset(and_1_out));  // open: Qn, preset, en
  T_Flip_Flop #(.trigger("falling")) t_ff_3 (
    .clk(out_5), .T(1'b1), .Q(out_4), .reset(and_1_out));  // open: Qn, preset, en
  T_Flip_Flop #(.trigger("falling")) t_ff_4 (
    .clk(out_4), .T(1'b1), .Q(out_2), .reset(and_1_out));  // open: Qn, preset, en
  and and_1 (and_1_out, out_2, ~out_4, out_5, ~out_6);  // AND_Gate

  assign out_3 = out_2;
endmodule

module Contador_Horas (
  input  in_1,
  output out_2,
  output out_3,
  output out_4,
  output out_5,
  output out_6,
  output out_7,
  output out_8,
  output out_9,
  output out_10
);

  wire and_1_out, and_2_out, and_3_out, and_4_out, and_5_out, or_1_out, or_2_out;

  T_Flip_Flop #(.trigger("falling")) t_ff_1 (
    .clk(in_1), .T(1'b1), .Q(out_8), .reset(or_1_out));  // open: Qn, preset, en
  or or_1 (or_1_out, and_2_out, and_1_out);
  T_Flip_Flop #(.trigger("falling")) t_ff_2 (
    .clk(out_8), .T(1'b1), .Q(out_7), .reset(or_1_out));  // open: Qn, preset, en
  T_Flip_Flop #(.trigger("falling")) t_ff_3 (
    .clk(out_7), .T(1'b1), .Q(out_6), .reset(or_1_out));  // open: Qn, preset, en
  and and_1 (and_1_out, and_3_out, and_5_out);
  T_Flip_Flop #(.trigger("falling")) t_ff_4 (
    .clk(out_6), .T(1'b1), .Q(out_5), .reset(or_1_out));  // open: Qn, preset, en
  and and_2 (and_2_out, out_5, ~out_6, out_7, ~out_8);  // AND_Gate
  and and_3 (and_3_out, ~out_5, out_6, ~out_7, ~out_8);  // AND_Gate
  or or_2 (or_2_out, and_1_out, and_4_out);
  T_Flip_Flop #(.trigger("falling")) t_ff_5 (
    .clk(out_5), .T(1'b1), .Q(out_4), .reset(or_2_out));  // open: Qn, preset, en
  T_Flip_Flop #(.trigger("falling")) t_ff_6 (
    .clk(out_4), .T(1'b1), .Q(out_2), .reset(or_2_out));  // open: Qn, preset, en
  and and_4 (and_4_out, out_2, out_4);
  and and_5 (and_5_out, out_2, ~out_4);  // AND_Gate

  assign out_3 = out_2;
  assign out_9 = 1'b0;
  assign out_10 = 1'b0;
endmodule

module decodificador (
  input  E1,
  input  E2,
  input  E3,
  input  E4,
  output a,
  output b,
  output c,
  output d,
  output e,
  output f,
  output g
);

  wire and_1_out, and_2_out, and_3_out, and_4_out, and_5_out, and_6_out, and_7_out, and_8_out, and_9_out,
       and_10_out, and_11_out, and_12_out, and_13_out, and_14_out, and_15_out, and_16_out, and_17_out,
       and_18_out, and_19_out, and_20_out, and_21_out, and_22_out, and_23_out, and_24_out, and_25_out,
       and_26_out, and_27_out, and_28_out, and_29_out, and_30_out, and_31_out, and_32_out, and_33_out,
       and_34_out, and_35_out, not_1_out, not_2_out, not_3_out, not_4_out, not_5_out, not_6_out, not_7_out,
       not_8_out, not_9_out, not_10_out, not_11_out, not_12_out, not_13_out, not_14_out, not_15_out,
       not_16_out, not_17_out, not_18_out, not_19_out, not_20_out, not_21_out, not_22_out, not_23_out,
       not_24_out, not_25_out, not_26_out, not_27_out, not_28_out, not_29_out, not_30_out, not_31_out,
       not_32_out, not_33_out, not_34_out, not_35_out, not_36_out, not_37_out, not_38_out, not_39_out,
       not_40_out, not_41_out, not_42_out, not_43_out;

  not not_1 (not_1_out, E2);
  not not_2 (not_2_out, E4);
  not not_3 (not_3_out, E1);
  not not_4 (not_4_out, E1);
  not not_5 (not_5_out, E2);
  not not_6 (not_6_out, E3);
  not not_7 (not_7_out, E4);
  not not_8 (not_8_out, E1);
  not not_9 (not_9_out, E2);
  not not_10 (not_10_out, E1);
  not not_11 (not_11_out, E3);
  not not_12 (not_12_out, E4);
  not not_13 (not_13_out, E2);
  not not_14 (not_14_out, E4);
  not not_15 (not_15_out, E1);
  not not_16 (not_16_out, E3);
  not not_17 (not_17_out, E1);
  not not_18 (not_18_out, E3);
  not not_19 (not_19_out, E1);
  not not_20 (not_20_out, E3);
  not not_21 (not_21_out, E1);
  not not_22 (not_22_out, E2);
  not not_23 (not_23_out, E1);
  not not_24 (not_24_out, E2);
  not not_25 (not_25_out, E4);
  not not_26 (not_26_out, E2);
  not not_27 (not_27_out, E3);
  not not_28 (not_28_out, E4);
  not not_29 (not_29_out, E3);
  not not_30 (not_30_out, E2);
  not not_31 (not_31_out, E4);
  not not_32 (not_32_out, E4);
  not not_33 (not_33_out, E3);
  not not_34 (not_34_out, E4);
  not not_35 (not_35_out, E1);
  not not_36 (not_36_out, E3);
  not not_37 (not_37_out, E4);
  not not_38 (not_38_out, E2);
  not not_39 (not_39_out, E2);
  not not_40 (not_40_out, E4);
  not not_41 (not_41_out, E1);
  not not_42 (not_42_out, E3);
  not not_43 (not_43_out, E2);
  and and_1 (and_1_out, not_1_out, not_2_out);
  and and_2 (and_2_out, not_3_out, E3);
  and and_3 (and_3_out, not_4_out, E2, E4);
  and and_4 (and_4_out, E2, E3);
  and and_5 (and_5_out, E1, not_5_out, not_6_out);
  and and_6 (and_6_out, E1, not_7_out);
  and and_7 (and_7_out, not_8_out, not_9_out);
  and and_8 (and_8_out, not_10_out, not_11_out, not_12_out);
  and and_9 (and_9_out, not_13_out, not_14_out);
  and and_10 (and_10_out, not_15_out, E3, E4);
  and and_11 (and_11_out, E1, not_16_out, E4);
  and and_12 (and_12_out, not_17_out, not_18_out);
  and and_13 (and_13_out, not_19_out, E4);
  and and_14 (and_14_out, not_20_out, E4);
  and and_15 (and_15_out, not_21_out, E2);
  and and_16 (and_16_out, E1, not_22_out);
  and and_17 (and_17_out, not_23_out, not_24_out, not_25_out);
  and and_18 (and_18_out, not_26_out, E3, E4);
  and and_19 (and_19_out, E2, not_27_out, E4);
  and and_20 (and_20_out, E2, E3, not_28_out);
  and and_21 (and_21_out, E1, not_29_out);
  and and_22 (and_22_out, not_30_out, not_31_out);
  and and_23 (and_23_out, E3, not_32_out);
  and and_24 (and_24_out, E1, E3);
  and and_25 (and_25_out, E1, E2);
  and and_26 (and_26_out, not_33_out, not_34_out);
  and and_27 (and_27_out, not_35_out, E2, not_36_out);
  and and_28 (and_28_out, E2, not_37_out);
  and and_29 (and_29_out, E1, not_38_out);
  and and_30 (and_30_out, E1, E3);
  and and_31 (and_31_out, not_39_out, E3);
  and and_32 (and_32_out, E3, not_40_out);
  and and_33 (and_33_out, not_41_out, E2, not_42_out);
  and and_34 (and_34_out, E1, not_43_out);
  and and_35 (and_35_out, E1, E4);
  or or_1 (a, and_1_out, and_2_out, and_3_out, and_4_out, and_5_out, and_6_out);
  or or_2 (b, and_7_out, and_8_out, and_9_out, and_10_out, and_11_out);
  or or_3 (c, and_12_out, and_13_out, and_14_out, and_15_out, and_16_out);
  or or_4 (d, and_17_out, and_18_out, and_19_out, and_20_out, and_21_out);
  or or_5 (e, and_22_out, and_23_out, and_24_out, and_25_out);
  or or_6 (f, and_26_out, and_27_out, and_28_out, and_29_out, and_30_out);
  or or_7 (g, and_31_out, and_32_out, and_33_out, and_34_out, and_35_out);
endmodule
