// Logisim project Somador  Ripple Carrier- 8 bit - Tiago Defendi (a2571374) - 2023.circ as structural Verilog: 3 circuits, main circuit main
module main (
  input  A,
  input  B,
  input  C_in,
  output S,
  output C_out
);

  wire and_1_out, and_2_out, and_3_out, xor_1_out;

  xor xor_1 (xor_1_out, B, C_in);
  and and_1 (and_1_out, A, B);
  and and_2 (and_2_out, A, C_in);
  and and_3 (and_3_out, B, C_in);
  xor xor_2 (S, xor_1_out, A);
  or or_1 (C_out, and_1_out, and_2_out, and_3_out);
endmodule

module Somador_Ripple_Carrier (
  input  A,
  input  A_2,
  input  A_3,
  input  A_4,
  input  A_5,
  input  A_6,
  input  A_7,
  input  A_8,
  input  B,
  input  B_2,
  input  B_3,
  input  B_4,
  input  B_5,
  input  B_6,
  input  B_7,
  input  B_8,
  input  in_17,
  output Overflow,
  output out_19,
  output out_20,
  output out_21,
  output out_22,
  output out_23,
  output out_24,
  output out_25,
  output out_26
);

  wire main_2_c_out, main_3_c_out, main_4_c_out, main_5_c_out, main_6_c_out, main_7_c_out, main_8_c_out;

  main main_1 (.S(out_19), .C_out(Overflow), .A(A), .B(B), .C_in(main_2_c_out));
  main main_2 (.S(out_20), .C_out(main_2_c_out), .A(A_2), .B(B_2), .C_in(main_4_c_out));
  main main_3 (.S(out_22), .C_out(main_3_c_out), .A(A_4), .B(B_4), .C_in(main_5_c_out));
  main main_4 (.S(out_21), .C_out(main_4_c_out), .A(A_3), .B(B_3), .C_in(main_3_c_out));
  main main_5 (.S(out_23), .C_out(main_5_c_out), .A(A_5), .B(B_5), .C_in(main_6_c_out));
  main main_6 (.S(out_24), .C_out(main_6_c_out), .A(A_6), .B(B_6), .C_in(main_8_c_out));
  main main_7 (.S(out_26), .C_out(main_7_c_out), .A(A_8), .B(B_8), .C_in(in_17));
  main main_8 (.S(out_25), .C_out(main_8_c_out), .A(A_7), .B(B_7), .C_in(main_7_c_out));
endmodule

module Somador (
  input  [7:0] in_1,
  input  [7:0] in_2,
  input  in_3,
  output [7:0] out_4
);

  wire somador_ripple_carrier_1_overflow;

  // Probe on in_1
  // Probe on in_2
  // Probe on out_4
  LED Overflow (.in(somador_ripple_carrier_1_overflow));
  Somador_Ripple_Carrier somador_ripple_carrier_1 (
    .Overflow(somador_ripple_carrier_1_overflow), .A(in_1[7]), .B(in_2[7]), .A_2(in_1[6]), .B_2(in_2[6]),
    .A_3(in_1[5]), .B_3(in_2[5]), .A_4(in_1[4]), .B_4(in_2[4]), .A_5(in_1[3]), .B_5(in_2[3]), .A_6(in_1[2]),
    .B_6(in_2[2]), .A_7(in_1[1]), .B_7(in_2[1]), .A_8(in_1[0]), .B_8(in_2[0]), .out_19(out_4[7]),
    .out_20(out_4[6]), .out_21(out_4[5]), .out_22(out_4[4]), .out_23(out_4[3]), .out_24(out_4[2]),
    .out_25(out_4[1]), .out_26(out_4[0]), .in_17(in_3));
endmodule
