// Logisim project ULA- 8 bits- Tiago Defendi (a2571374) - 2023.circ as structural Verilog: 5 circuits, main circuit main
module main (
  input  [7:0] A,
  input  [7:0] B,
  input  [2:0] Op,
  output [7:0] out_4
);

  wire [7:0] and_1_out, and_2_out, and_3_out, and_4_out, and_5_out, and_6_out, and_7_out, and_8_out,
       divider_1_out, divider_1_rem, multiplier_1_out, operador_1_out_2, operador_1_out_3, operador_1_out_4,
       operador_1_out_5, operador_1_out_6, operador_1_out_7, operador_1_out_8, operador_1_out_9, or_1_out,
       or_3_out, somador_look_ahead_1_out_4, xor_1_out;

  // Probe on A
  // Probe on B
  Operador operador_1 (
    .\Operação (Op), .out_2(operador_1_out_2), .out_3(operador_1_out_3), .out_4(operador_1_out_4),
    .out_5(operador_1_out_5), .out_6(operador_1_out_6), .out_7(operador_1_out_7), .out_8(operador_1_out_8),
    .out_9(operador_1_out_9));
  assign and_1_out = operador_1_out_2 & and_2_out;  // AND_Gate and_1, 8 bits wide
  assign and_2_out = A & B;  // AND_Gate and_2, 8 bits wide
  assign or_1_out = A | B;  // OR_Gate or_1, 8 bits wide
  assign and_3_out = operador_1_out_3 & or_1_out;  // AND_Gate and_3, 8 bits wide
  assign out_4 = and_1_out | and_3_out | and_4_out | and_5_out | and_6_out | and_8_out | and_7_out;  // OR_Gate or_2, 8 bits wide
  // Probe on out_4
  assign xor_1_out = A ^ B;  // XOR_Gate xor_1, 8 bits wide
  assign and_4_out = operador_1_out_4 & xor_1_out;  // AND_Gate and_4, 8 bits wide
  assign or_3_out = operador_1_out_5 | operador_1_out_6;  // OR_Gate or_3, 8 bits wide
  Somador_Look_Ahead somador_look_ahead_1 (
    .A(A), .B(B), .in_2(operador_1_out_6[4]), .out_4(somador_look_ahead_1_out_4));
  assign and_5_out = or_3_out & somador_look_ahead_1_out_4;  // AND_Gate and_5, 8 bits wide
  Multiplier multiplier_1 (.a(A), .b(B), .out(multiplier_1_out));  // open: cin, cout
  assign and_6_out = operador_1_out_7 & multiplier_1_out;  // AND_Gate and_6, 8 bits wide
  Divider divider_1 (.a(A), .b(B), .out(divider_1_out), .rem(divider_1_rem));  // open: upper
  assign and_7_out = operador_1_out_9 & divider_1_rem;  // AND_Gate and_7, 8 bits wide
  assign and_8_out = operador_1_out_8 & divider_1_out;  // AND_Gate and_8, 8 bits wide
endmodule

module Operador (
  input  [2:0] \Operação ,
  output [7:0] out_2,
  output [7:0] out_3,
  output [7:0] out_4,
  output [7:0] out_5,
  output [7:0] out_6,
  output [7:0] out_7,
  output [7:0] out_8,
  output [7:0] out_9
);

  and and_1 (out_2[7], ~\Operação [2], ~\Operação [1], ~\Operação [0]);  // AND_Gate
  and and_2 (out_3[7], ~\Operação [2], ~\Operação [1], \Operação [0]);  // AND_Gate
  and and_3 (out_4[7], ~\Operação [2], \Operação [1], ~\Operação [0]);  // AND_Gate
  and and_4 (out_5[7], ~\Operação [2], \Operação [1], \Operação [0]);  // AND_Gate
  and and_5 (out_6[7], \Operação [2], ~\Operação [1], ~\Operação [0]);  // AND_Gate
  and and_6 (out_7[7], \Operação [2], ~\Operação [1], \Operação [0]);  // AND_Gate
  and and_7 (out_8[7], \Operação [2], \Operação [1], ~\Operação [0]);  // AND_Gate
  and and_8 (out_9[7], \Operação [2], \Operação [1], \Operação [0]);

  assign out_2[6:0] = {7{out_2[7]}};
  assign out_3[6:0] = {7{out_3[7]}};
  assign out_4[6:0] = {7{out_4[7]}};
  assign out_5[6:0] = {7{out_5[7]}};
  assign out_6[6:0] = {7{out_6[7]}};
  assign out_7[6:0] = {7{out_7[7]}};
  assign out_8[6:0] = {7{out_8[7]}};
  assign out_9[6:0] = {7{out_9[7]}};
endmodule

module Somador_Look_Ahead (
  input  [7:0] A,
  input  in_2,
  input  [7:0] B,
  output [7:0] out_4
);

  wire and_1_out, and_2_out, and_3_out, and_4_out, and_5_out, and_6_out, and_7_out, and_8_out, and_9_out,
       and_10_out, and_11_out, and_12_out, and_13_out, and_14_out, and_15_out, and_16_out, and_17_out,
       and_18_out, and_19_out, and_20_out, and_21_out, and_22_out, and_23_out, and_24_out, and_25_out,
       and_26_out, and_27_out, and_28_out, and_29_out, and_30_out, and_31_out, and_32_out, and_33_out,
       and_34_out, and_35_out, and_36_out, G0___P0_g__a_b, G0___P0_p__a_b, G1___P1_g__a_b, G1___P1_p__a_b,
       G2___P2_g__a_b, G2___P2_p__a_b, G3___P3_g__a_b, G3___P3_p__a_b, G4___P4_g__a_b, G4___P4_p__a_b,
       G5___P5_g__a_b, G5___P5_p__a_b, G6___P6_g__a_b, G6___P6_p__a_b, G7___P7_g__a_b, G7___P7_p__a_b,
       or_1_out, or_2_out, or_3_out, or_4_out, or_5_out, or_6_out, or_7_out, or_8_out;
  wire [7:0] xor_1_out;

  // Probe on out_4
  // Probe on A
  // Probe on xor_1_out
  assign xor_1_out = B ^ {8{in_2}};  // XOR_Gate xor_1, 8 bits wide
  GePeto G0___P0 (.G__A_B(G0___P0_g__a_b), .P__A_B(G0___P0_p__a_b), .A(A[0]), .B(xor_1_out[0]));
  GePeto G1___P1 (.G__A_B(G1___P1_g__a_b), .P__A_B(G1___P1_p__a_b), .A(A[1]), .B(xor_1_out[1]));
  GePeto G2___P2 (.G__A_B(G2___P2_g__a_b), .P__A_B(G2___P2_p__a_b), .A(A[2]), .B(xor_1_out[2]));
  GePeto G3___P3 (.G__A_B(G3___P3_g__a_b), .P__A_B(G3___P3_p__a_b), .A(A[3]), .B(xor_1_out[3]));
  GePeto G4___P4 (.G__A_B(G4___P4_g__a_b), .P__A_B(G4___P4_p__a_b), .A(A[4]), .B(xor_1_out[4]));
  GePeto G5___P5 (.G__A_B(G5___P5_g__a_b), .P__A_B(G5___P5_p__a_b), .A(A[5]), .B(xor_1_out[5]));
  GePeto G6___P6 (.G__A_B(G6___P6_g__a_b), .P__A_B(G6___P6_p__a_b), .A(A[6]), .B(xor_1_out[6]));
  GePeto G7___P7 (.G__A_B(G7___P7_g__a_b), .P__A_B(G7___P7_p__a_b), .A(A[7]), .B(xor_1_out[7]));
  and and_1 (and_1_out, G7___P7_p__a_b, G6___P6_p__a_b, G5___P5_g__a_b);
  and and_2 (and_2_out, G7___P7_p__a_b, G6___P6_g__a_b);
  or or_1 (or_1_out, G7___P7_g__a_b, and_2_out, and_1_out, and_3_out, and_4_out, and_5_out, and_6_out, and_7_out, and_8_out);
  LED Overflow (.in(or_1_out));
  and and_3 (and_3_out, G7___P7_p__a_b, G6___P6_p__a_b, G5___P5_p__a_b, G4___P4_g__a_b);
  and and_4 (and_4_out, G7___P7_p__a_b, G6___P6_p__a_b, G5___P5_p__a_b, G4___P4_p__a_b, G3___P3_g__a_b);
  and and_5 (and_5_out, G7___P7_p__a_b, G6___P6_p__a_b, G5___P5_p__a_b, G4___P4_p__a_b, G3___P3_p__a_b, G2___P2_g__a_b);
  and and_6 (and_6_out, G7___P7_p__a_b, G6___P6_p__a_b, G5___P5_p__a_b, G4___P4_p__a_b, G3___P3_p__a_b, G2___P2_p__a_b, G1___P1_g__a_b);
  and and_7 (and_7_out, G7___P7_p__a_b, G6___P6_p__a_b, G5___P5_p__a_b, G4___P4_p__a_b, G3___P3_p__a_b, G2___P2_p__a_b, G1___P1_p__a_b, G0___P0_g__a_b);
  and and_8 (and_8_out, G7___P7_p__a_b, G6___P6_p__a_b, G5___P5_p__a_b, G4___P4_p__a_b, G3___P3_p__a_b, G2___P2_p__a_b, G1___P1_p__a_b, G0___P0_p__a_b, in_2);
  Somador_de_1_bit somador_de_1_bit_1 (.S(out_4[7]), .A(A[7]), .B(xor_1_out[7]), .C_in(or_2_out));
  and and_9 (and_9_out, G6___P6_p__a_b, G5___P5_p__a_b, G4___P4_g__a_b);
  and and_10 (and_10_out, G6___P6_p__a_b, G5___P5_g__a_b);
  or or_2 (or_2_out, G6___P6_g__a_b, and_10_out, and_9_out, and_11_out, and_12_out, and_13_out, and_14_out, and_15_out);
  and and_11 (and_11_out, G6___P6_p__a_b, G5___P5_p__a_b, G4___P4_p__a_b, G3___P3_g__a_b);
  and and_12 (and_12_out, G6___P6_p__a_b, G5___P5_p__a_b, G4___P4_p__a_b, G3___P3_p__a_b, G2___P2_g__a_b);
  and and_13 (and_13_out, G6___P6_p__a_b, G5___P5_p__a_b, G4___P4_p__a_b, G3___P3_p__a_b, G2___P2_p__a_b, G1___P1_g__a_b);
  and and_14 (and_14_out, G6___P6_p__a_b, G5___P5_p__a_b, G4___P4_p__a_b, G3___P3_p__a_b, G2___P2_p__a_b, G1___P1_p__a_b, G0___P0_g__a_b);
  and and_15 (and_15_out, G6___P6_p__a_b, G5___P5_p__a_b, G4___P4_p__a_b, G3___P3_p__a_b, G2___P2_p__a_b, G1___P1_p__a_b, G0___P0_p__a_b, in_2);
  and and_16 (and_16_out, G5___P5_p__a_b, G4___P4_g__a_b);
  or or_3 (or_3_out, G5___P5_g__a_b, and_16_out, and_17_out, and_18_out, and_19_out, and_20_out, and_21_out);
  Somador_de_1_bit somador_de_1_bit_2 (.S(out_4[6]), .A(A[6]), .B(xor_1_out[6]), .C_in(or_3_out));
  and and_17 (and_17_out, G5___P5_p__a_b, G4___P4_p__a_b, G3___P3_g__a_b);
  and and_18 (and_18_out, G5___P5_p__a_b, G4___P4_p__a_b, G3___P3_p__a_b, G2___P2_g__a_b);
  and and_19 (and_19_out, G5___P5_p__a_b, G4___P4_p__a_b, G3___P3_p__a_b, G2___P2_p__a_b, G1___P1_g__a_b);
  and and_20 (and_20_out, G5___P5_p__a_b, G4___P4_p__a_b, G3___P3_p__a_b, G2___P2_p__a_b, G1___P1_p__a_b, G0___P0_g__a_b);
  and and_21 (and_21_out, G5___P5_p__a_b, G4___P4_p__a_b, G3___P3_p__a_b, G2___P2_p__a_b, G1___P1_p__a_b, G0___P0_p__a_b, in_2);
  Somador_de_1_bit somador_de_1_bit_3 (.S(out_4[5]), .A(A[5]), .B(xor_1_out[5]), .C_in(or_4_out));
  and and_22 (and_22_out, G4___P4_p__a_b, G3___P3_g__a_b);
  and and_23 (and_23_out, G4___P4_p__a_b, G3___P3_p__a_b, G2___P2_g__a_b);
  or or_4 (or_4_out, G4___P4_g__a_b, and_22_out, and_23_out, and_24_out, and_25_out, and_26_out);
  and and_24 (and_24_out, G4___P4_p__a_b, G3___P3_p__a_b, G2___P2_p__a_b, G1___P1_g__a_b);
  and and_25 (and_25_out, G4___P4_p__a_b, G3___P3_p__a_b, G2___P2_p__a_b, G1___P1_p__a_b, G0___P0_g__a_b);
  and and_26 (and_26_out, G4___P4_p__a_b, G3___P3_p__a_b, G2___P2_p__a_b, G1___P1_p__a_b, G0___P0_p__a_b, in_2);
  Somador_de_1_bit somador_de_1_bit_4 (.S(out_4[4]), .A(A[4]), .B(xor_1_out[4]), .C_in(or_5_out));
  and and_27 (and_27_out, G3___P3_p__a_b, G2___P2_p__a_b, G1___P1_g__a_b);
  and and_28 (and_28_out, G3___P3_p__a_b, G2___P2_g__a_b);
  or or_5 (or_5_out, G3___P3_g__a_b, and_28_out, and_27_out, and_29_out, and_30_out);
  and and_29 (and_29_out, G3___P3_p__a_b, G2___P2_p__a_b, G1___P1_p__a_b, G0___P0_g__a_b);
  and and_30 (and_30_out, G3___P3_p__a_b, G2___P2_p__a_b, G1___P1_p__a_b, G0___P0_p__a_b, in_2);
  Somador_de_1_bit somador_de_1_bit_5 (.S(out_4[3]), .A(A[3]), .B(xor_1_out[3]), .C_in(or_6_out));
  and and_31 (and_31_out, G2___P2_p__a_b, G1___P1_p__a_b, G0___P0_g__a_b);
  and and_32 (and_32_out, G2___P2_p__a_b, G1___P1_g__a_b);
  or or_6 (or_6_out, G2___P2_g__a_b, and_32_out, and_31_out, and_33_out);
  and and_33 (and_33_out, G2___P2_p__a_b, G1___P1_p__a_b, G0___P0_p__a_b, in_2);
  Somador_de_1_bit somador_de_1_bit_6 (.S(out_4[2]), .A(A[2]), .B(xor_1_out[2]), .C_in(or_7_out));
  and and_34 (and_34_out, G1___P1_p__a_b, G0___P0_g__a_b);
  and and_35 (and_35_out, G1___P1_p__a_b, G0___P0_p__a_b, in_2);
  or or_7 (or_7_out, G1___P1_g__a_b, and_34_out, and_35_out);
  and and_36 (and_36_out, G0___P0_p__a_b, in_2);
  or or_8 (or_8_out, G0___P0_g__a_b, and_36_out);
  Somador_de_1_bit somador_de_1_bit_7 (.S(out_4[1]), .A(A[1]), .B(xor_1_out[1]), .C_in(or_8_out));
  Somador_de_1_bit somador_de_1_bit_8 (.S(out_4[0]), .A(A[0]), .B(xor_1_out[0]), .C_in(in_2));
endmodule

module Somador_de_1_bit (
  input  A,
  input  B,
  input  C_in,
  output S
);

  wire xor_1_out;

  xor xor_1 (xor_1_out, B, C_in);
  xor xor_2 (S, A, xor_1_out);
endmodule

module GePeto (
  input  A,
  input  B,
  output G__A_B,
  output P__A_B
);

  and and_1 (G__A_B, A, B);
  or or_1 (P__A_B, A, B);
endmodule
